# Fritzing sketch raspi_adapter (saved by Fritzing 0.9.3b)
circuit board: 8.46667cm x 5.64444cm
breadboards: 1

parts:
  Raspberry_Pi_1 = Raspberry Pi 3 [part_number=RPI-3-V1.2]
  Componente1 = Arduino Prototyping Shield
  Q1 = NPN-Transistor [package="TO92 [THT]"]
  R1 = Resistor [tolerance=±5% resistance=220 package=THT]
  Q2 = NPN-Transistor [package="TO92 [THT]"]
  R2 = Resistor [tolerance=±5% resistance=220 package=THT]
  Q3 = NPN-Transistor [package="TO92 [THT]"]
  R3 = Resistor [tolerance=±5% resistance=220 package=THT]

nets:
  3V3: Raspberry_Pi_1.3v3, Raspberry_Pi_1.3V3, Q1.B, Q2.B, Q3.B
  GND: Raspberry_Pi_1.GND, Componente1.GND
  N1: Raspberry_Pi_1.GIPO25, Q3.E
  N2: Raspberry_Pi_1.GIPO24, Q2.E
  N3: Raspberry_Pi_1.GIPO23, Q1.E
  5V: Raspberry_Pi_1.5V, Componente1.+5V, R1.Pin_0, R2.Pin_0, R3.Pin_0
  N4: Componente1.D8, Q3.C, R3.Pin_1
  N5: Componente1.D3, Q2.C, R2.Pin_1
  N6: Componente1.D7, Q1.C, R1.Pin_1
